# Fritzing sketch LED-Configuration-System (saved by Fritzing 0.9.4)
breadboards: 1

parts:
  LCD1 = LCD screen
  Part1 = Arduino Uno (Rev3) - ICSP  # not connected
  R1 = Resistor [tolerance=±5% resistance=220 package="0603 [SMD]"]
  R2 = Trimmer Potentiometer [maximum_resistance=10kΩ package=THT]
  LED1 = smd LED [color="Red (633nm)" package="1206 [SMD]"]
  R3 = Resistor [tolerance=±5% resistance=220 package="0603 [SMD]"]

nets:
  N1: LCD1.VSS, LCD1.R/W, LCD1.LED-, R2.leg1, LED1.cathode
  N2: R1.Pin_0, R2.leg2, R3.Pin_0
  N3: LED1.anode, R3.Pin_1

notes:
  Arduino UNO
  220 OHM
  Red LED
  Potentiometer
  16x2 LCD
